# Fritzing sketch ardufocus1 (saved by Fritzing 0.8.3b)
breadboards: 1

parts:
  DRV1 = A4983
  S1 = Pushbutton [package="[THT]"]  # not connected
  S3 = Pushbutton [package="[THT]"]  # not connected
  S4 = Pushbutton [package="[THT]"]  # not connected
  S5 = Pushbutton [package="[THT]"]  # not connected
  S6 = Pushbutton [package="[THT]"]  # not connected
  Parte2 = DeuLigne 1.1 - The Snootlab's LCD shield for Arduino
  Parte3 = Arduino Mega 2560 (Rev3)
  R1 = Rotary Potentiometer (Large) [maximum_resistance=100kΩ package=THT]
  U1 = POT [package=pot_mammoth]
  LED1 = LED - 3mm [color="Red (633nm)" package="3 mm [THT]"]
  S7 = Square Pushbutton
  M1 = Stepper Motor - Bipolar
  T1 = LM35 Temperature Sensor [package="TO92 [THT]"]
  BAT1 = BC9VPC [package=bc9vpc]
  R2 = Resistor [tolerance=±5% resistance=220 package=THT]
  R3 = Resistor [tolerance=±5% resistance=220 package=THT]
  R5 = Resistor [tolerance=±5% resistance=220 package=THT]
  R6 = Resistor [tolerance=±5% resistance=2.2k package=THT]

nets:
  N1: DRV1.SLP, Parte3.D26
  N2: DRV1.STEP, Parte3.D24
  N3: DRV1.DIR, Parte3.D2_PWM
  N4: DRV1.VMOT, BAT1.V-
  N5: DRV1.GNDMOT, BAT1.V+
  N6: DRV1.2B, M1.A
  N7: DRV1.2A, M1.C
  N8: DRV1.1A, M1.B
  N9: DRV1.1B, M1.D
  VDD: DRV1.VDD, Parte2.+5V, Parte3.5V, R1.leg1, U1.S, R5.Pin_1, R6.Pin_1
  GND: DRV1.GND, Parte2.GND, Parte3.GND, LED1.cathode, T1.GND, R2.Pin_1
  N10: Parte2.A0, Parte3.A0
  N11: Parte2.D4, Parte3.D4_PWM
  N12: Parte2.D8, Parte3.D8_PWM
  N13: Parte2.D9, Parte3.D9_PWM
  N14: Parte2.D10_SS, Parte3.D10_PWM
  N15: Parte2.D5, Parte3.D5_PWM
  N16: Parte2.D6, Parte3.D6_PWM
  N17: Parte2.D7, Parte3.D7_PWM
  N18: Parte3.A8, T1.Vout, R6.Pin_0
  N19: Parte3.A1, U1.A
  N20: Parte3.A3, R1.wiper
  N21: Parte3.D3_PWM, S7.leg0
  N22: Parte3.D50, LED1.anode
  N23: R1.leg2, R3.Pin_0
  N24: U1.E, R2.Pin_0

notes:
  Control pasos del
  ajuste fino
  Control de velocidad
  Control fin de carrera.
  Botonera:
  Usa multeplexacion por resistencias
  puerto A0
  Brillo de la LCD pin 10
  O fuente alimentación 12V

custom parts:
  A4983: Poloko A4983 Stepper Motor Control Breakout
