# Fritzing sketch ardufocuser2 (saved by Fritzing 0.7.12b)
perfboards: 2

parts:
  LCD1 = LCD screen
  J1 = Generic female header - 10 pins [package=THT]
  J2 = Generic female header - 4 pins [package=THT]
  M1 = Stepper Motor - Bipolar
  Arduino1 = Arduino  # not connected
  DRV2 = A4983
  C2 = Electrolytic Capacitor [capacitance=0.1mF voltage=16V package="100 mil [THT, electrolytic]"]
  J4 = male pin header, 2 pins [form="♂ (male)"]
  J6 = male pin header, 2 pins [form="♂ (male)"]
  J9 = male pin header, 2 pins [form="♂ (male)"]
  J11 = male pin header, 7 pins [form="♂ (male)"]
  J13 = male pin header, 10 pins [form="♂ (male)"]
  R2 = Trimmer Potentiometer [maximum_resistance=10kΩ package=THT]
  R3 = Resistor [tolerance=±5% resistance=47 package="0603 [SMD]"]
  R5 = Rotary Potentiometer (Small) [maximum_resistance=100kΩ]
  J14 = female pin header, 7 pins [form="♀ (female)"]
  J12 = male pin header, 7 pins [form="♂ (male)"]
  J3 = male pin header, 8 pins [form="♂ (male)"]
  J7 = female pin header, 2 pins [form="♀ (female)"]
  J5 = female pin header, 2 pins [form="♀ (female)"]
  J10 = male pin header, 2 pins [form="♂ (male)"]
  J8 = female pin header, 2 pins [form="♀ (female)"]
  J15 = female pin header, 3 pins [form="♀ (female)"]
  J16 = female pin header, 3 pins [form="♀ (female)"]
  R6 = Rotary Potentiometer (Small) [maximum_resistance=100kΩ]
  J17 = male pin header, 3 pins [form="♂ (male)"]
  J18 = male pin header, 3 pins [form="♂ (male)"]
  J19 = male pin header, 2 pins [form="♂ (male)"]
  J20 = female pin header, 2 pins [form="♀ (female)"]
  J21 = male pin header, 2 pins [form="♂ (male)"]
  R9 = 470 Ω Resistor [package=THT]
  J24 = male pin header, 4 pins [form="♂ (male)"]
  J22 = longpad pin header, 3 pins [form="long pad"]
  J25 = Generic female header - 3 pins [package=THT]
  J26 = Generic male header - 3 pins [package=THT]
  J27 = Generic female header - 4 pins [package=THT]
  J28 = male pin header, 1 pin [form="♂ (male)"]
  J29 = Generic female header - 3 pins [package=THT]
  J30 = Generic male header - 3 pins [package=THT]
  T1 = LM35 Temperature Sensor [package="TO92 [THT]"]
  J31 = Generic male header [package=THT]
  J32 = female pin header, 1 pin [form="♀ (female)"]
  S4 = Round Pushbutton
  J33 = Generic male header - 3 pins [package=THT]
  J34 = Generic male header - 2 pins [package=THT]
  R14 = Resistor [tolerance=±5% resistance=47 package="0603 [SMD]"]
  R15 = Resistor [tolerance=±5% resistance=47 package="0603 [SMD]"]
  R16 = Resistor [tolerance=±5% resistance=47 package="0603 [SMD]"]
  R17 = Resistor [tolerance=±5% resistance=47 package="0603 [SMD]"]
  J35 = Generic male header - 2 pins [package=THT]
  J36 = Generic male header - 2 pins [package=THT]
  J37 = Generic male header - 2 pins [package=THT]
  R18 = Resistor [tolerance=±5% resistance=10k package="0603 [SMD]"]
  R19 = Resistor [tolerance=±5% resistance=330 package="0603 [SMD]"]
  J38 = Generic male header - 2 pins [package=THT]
  LED1 = LED - 3mm [color="Red (633nm)" package="3 mm [THT]"]
  J39 = Generic female header - 2 pins [package=THT]
  J41 = Generic female header - 2 pins [package=THT]
  J44 = Generic female header - 3 pins [package=THT]
  J45 = longpad pin header, 3 pins [form="long pad"]
  J46 = Generic female header - 3 pins [package=THT]
  J47 = Generic female header - 4 pins [package=THT]
  R20 = 10k Ω Resistor [package=THT]  # not connected
  R21 = 10k Ω Resistor [package=THT]  # not connected
  J48 = male pin header, 2 pins [form="♂ (male)"]
  J49 = male pin header, 2 pins [form="♂ (male)"]
  J50 = male pin header, 2 pins [form="♂ (male)"]
  S5 = Round Pushbutton
  J51 = Generic female header - 2 pins [package=THT]
  J52 = female pin header, 2 pins [form="♀ (female)"]
  J53 = male pin header, 2 pins [form="♂ (male)"]
  R22 = Resistor [tolerance=±5% resistance=220 package="0603 [SMD]"]
  J54 = male pin header, 2 pins [form="♂ (male)"]
  LED2 = LED - 3mm [color="Red (633nm)" package="3 mm [THT]"]
  J55 = female pin header, 2 pins [form="♀ (female)"]

nets:
  N1: LCD1.VSS, LCD1.R/W
  N2: LCD1.VDD, J1.pin1
  N3: LCD1.V0, J1.pin2
  N4: LCD1.RS, J1.pin3
  N5: LCD1.E, J1.pin4
  N6: LCD1.DB4, J1.pin5
  N7: LCD1.DB5, J1.pin6
  N8: LCD1.DB6, J1.pin7
  N9: LCD1.DB7, J1.pin8
  N10: LCD1.LED+, J1.pin9
  N11: LCD1.LED-, J1.pin10
  N12: J2.pin1, M1.D
  N13: J2.pin2, M1.B
  N14: J2.pin3, M1.C
  N15: J2.pin4, M1.A
  N16: DRV2.EN, R2.leg2
  N17: DRV2.STEP, J10.pin1
  N18: DRV2.DIR, J10.pin2
  N19: DRV2.2B, J3.pin3
  N20: DRV2.2A, J3.pin4
  N21: DRV2.1A, J3.pin5
  N22: DRV2.1B, J3.pin6
  N23: C2.-, J3.pin1
  N24: J4.pin1, J5.pin1
  N25: J4.pin2, J5.pin2
  N26: J6.pin1, J7.pin2
  N27: J6.pin2, J7.pin1
  N28: J9.pin1, J8.pin1
  N29: J9.pin2, J8.pin2
  N30: J11.pin1, J14.pin7
  N31: J11.pin2, J14.pin6
  N32: J11.pin3, J14.pin5
  N33: J11.pin4, J14.pin4
  N34: J11.pin5, J14.pin3
  N35: J11.pin6, J14.pin2
  N36: J11.pin7, J14.pin1
  N37: J13.pin2, R3.Pin_0
  N38: J13.pin3, J12.pin2
  N39: J13.pin4, J12.pin3
  N40: J13.pin5, J12.pin4
  N41: J13.pin6, J12.pin5
  N42: J13.pin7, J12.pin6
  N43: J13.pin8, J12.pin7
  N44: J13.pin9, R2.wiper
  N45: R2.leg1, J18.pin1
  N46: R5.leg1, J15.pin1
  N47: R5.wiper, J15.pin2
  N48: R5.leg2, J15.pin3
  N49: J3.pin2, J30.pin3
  N50: J3.pin7, J17.pin3
  N51: J3.pin8, J18.pin3
  N52: J16.pin1, R6.leg1
  N53: J16.pin2, R6.wiper
  N54: J16.pin3, R6.leg2
  N55: J17.pin2, J19.pin2
  N56: J18.pin2, J19.pin1
  N57: J20.pin1, J21.pin2
  N58: J20.pin2, J21.pin1
  N59: R9.Pin_0, J24.pin1
  N60: J24.pin3, J22.pin1
  N61: J24.pin4, J22.pin2
  N62: J22.pin3, J45.pin3
  N63: J25.pin1, J26.pin3
  N64: J25.pin2, J26.pin2
  N65: J25.pin3, J26.pin1
  N66: J27.pin1, J47.pin1
  N67: J27.pin2, J47.pin2
  N68: J27.pin3, J47.pin3
  N69: J27.pin4, J47.pin4
  N70: J28.pin1, J32.pin1
  N71: J29.pin1, T1.+Vs
  N72: J29.pin2, T1.Vout
  N73: J29.pin3, T1.GND
  N74: J30.pin2, J31.pin1
  N75: S4.leg0, J41.pin1
  N76: S4.leg1, J41.pin2
  N77: J33.pin1, R19.Pin_1
  N78: J33.pin2, R18.Pin_1
  N79: J34.pin2, R17.Pin_0
  N80: R14.Pin_0, J37.pin2
  N81: R15.Pin_0, J36.pin2
  N82: R16.Pin_0, J35.pin2
  N83: R18.Pin_0, J38.pin2
  N84: R19.Pin_0, J38.pin1
  N85: LED1.cathode, J39.pin2
  N86: LED1.anode, J39.pin1
  N87: J44.pin1, J46.pin3
  N88: J44.pin2, J46.pin1
  N89: J44.pin3, J46.pin2
  N90: J48.pin2, J50.pin2
  N91: J49.pin2, J50.pin1
  N92: S5.leg0, J51.pin1
  N93: S5.leg1, J51.pin2
  N94: J52.pin1, J53.pin1
  N95: J52.pin2, J53.pin2
  N96: R22.Pin_1, J54.pin2
  N97: LED2.anode, J55.pin2

notes:
  Nunchaku
  x2
  x4

custom parts:
  A4983: Poloko A4983 Stepper Motor Control Breakout
