# Fritzing sketch ardufocuser3 (saved by Fritzing 0.8.5b)
perfboards: 3

parts:
  J1 = Generic female header - 10 pins [package=THT]
  J2 = Generic female header - 4 pins [package=THT]
  M1 = Stepper Motor - Bipolar
  DRV2 = A4983
  C2 = Electrolytic Capacitor [capacitance=0.1mF voltage=16V package="100 mil [THT, electrolytic]"]
  J4 = male pin header, 2 pins [form="♂ (male)"]
  J6 = male pin header, 2 pins [form="♂ (male)"]
  J9 = male pin header, 2 pins [form="♂ (male)"]
  J11 = male pin header, 7 pins [form="♂ (male)"]
  J13 = male pin header, 10 pins [form="♂ (male)"]
  R2 = Trimmer Potentiometer [maximum_resistance=10kΩ package=THT]
  R3 = Resistor [tolerance=±5% resistance=47 package="0603 [SMD]"]
  J14 = female pin header, 7 pins [form="♀ (female)"]
  J12 = male pin header, 7 pins [form="♂ (male)"]
  J3 = male pin header, 8 pins [form="♂ (male)"]
  J7 = female pin header, 2 pins [form="♀ (female)"]
  J5 = female pin header, 2 pins [form="♀ (female)"]
  J10 = male pin header, 2 pins [form="♂ (male)"]
  J8 = female pin header, 2 pins [form="♀ (female)"]
  J15 = female pin header, 3 pins [form="♀ (female)"]
  J16 = female pin header, 3 pins [form="♀ (female)"]
  J17 = male pin header, 3 pins [form="♂ (male)"]
  J18 = male pin header, 3 pins [form="♂ (male)"]
  J19 = male pin header, 2 pins [form="♂ (male)"]  # not connected
  J20 = female pin header, 2 pins [form="♀ (female)"]
  J21 = male pin header, 2 pins [form="♂ (male)"]
  J24 = male pin header, 4 pins [form="♂ (male)"]
  J22 = longpad pin header, 3 pins [form="long pad"]
  J27 = Generic female header - 4 pins [package=THT]
  J28 = male pin header, 1 pin [form="♂ (male)"]
  T1 = LM35 Temperature Sensor [package="TO92 [THT]"]
  J32 = female pin header, 1 pin [form="♀ (female)"]
  S4 = Round Pushbutton
  R14 = Resistor [tolerance=±5% resistance=4.7k package="0603 [SMD]"]
  R15 = Resistor [tolerance=±5% resistance=2.2k package="0603 [SMD]"]
  R16 = Resistor [tolerance=±5% resistance=1k package="0603 [SMD]"]
  R17 = Resistor [tolerance=±5% resistance=470 package="0603 [SMD]"]
  R18 = Resistor [tolerance=±5% resistance=10k package="0603 [SMD]"]
  R19 = Resistor [tolerance=±5% resistance=1k package="0603 [SMD]"]
  LED1 = LED - 3mm [color="Red (633nm)" package="3 mm [THT]"]
  J45 = longpad pin header, 3 pins [form="long pad"]
  J47 = Generic female header - 4 pins [package=THT]
  J48 = male pin header, 2 pins [form="♂ (male)"]
  J49 = male pin header, 2 pins [form="♂ (male)"]
  J50 = male pin header, 2 pins [form="♂ (male)"]
  S5 = Round Pushbutton
  J52 = female pin header, 2 pins [form="♀ (female)"]
  J53 = male pin header, 2 pins [form="♂ (male)"]
  R22 = Resistor [tolerance=±5% resistance=1k package="0603 [SMD]"]
  J54 = male pin header, 2 pins [form="♂ (male)"]
  LED2 = LED - 3mm [color="Red (633nm)" package="3 mm [THT]"]
  J55 = female pin header, 2 pins [form="♀ (female)"]
  DRV3 = A4983
  J56 = male pin header, 8 pins [form="♂ (male)"]
  J57 = female pin header, 8 pins [form="♀ (female)"]
  J58 = female pin header, 8 pins [form="♀ (female)"]
  J59 = male pin header, 2 pins [form="♂ (male)"]
  J60 = male pin header, 2 pins [form="♂ (male)"]
  J61 = male pin header, 3 pins [form="♂ (male)"]
  J62 = male pin header, 3 pins [form="♂ (male)"]
  R23 = Trimmer Potentiometer [maximum_resistance=10kΩ package=THT]
  J63 = male pin header, 10 pins [form="♂ (male)"]
  J64 = male pin header, 7 pins [form="♂ (male)"]
  J65 = longpad pin header, 3 pins [form="long pad"]
  J66 = male pin header, 4 pins [form="♂ (male)"]
  J67 = male pin header, 2 pins [form="♂ (male)"]
  J68 = longpad pin header, 3 pins [form="long pad"]
  J69 = male pin header, 2 pins [form="♂ (male)"]
  J70 = male pin header, 2 pins [form="♂ (male)"]
  J73 = male pin header, 2 pins [form="♂ (male)"]
  R25 = Resistor [tolerance=±5% resistance=1k package="0603 [SMD]"]
  R26 = Resistor [tolerance=±5% resistance=47 package="0603 [SMD]"]
  J71 = male pin header, 3 pins [form="♂ (male)"]
  R24 = Resistor [tolerance=±5% resistance=470 package=THT]  # not connected
  J36 = male pin header, 2 pins [form="♂ (male)"]
  J37 = male pin header, 2 pins [form="♂ (male)"]
  J35 = male pin header, 2 pins [form="♂ (male)"]
  R28 = Resistor [tolerance=±5% resistance=10k package=THT]  # not connected
  J72 = male pin header, 1 pin [form="♂ (male)"]
  J34 = male pin header, 2 pins [form="♂ (male)"]
  R27 = Resistor [tolerance=±5% resistance=10k package=THT]  # not connected
  R21 = Resistor [tolerance=±5% resistance=10k package=THT]  # not connected
  J33 = male pin header, 3 pins [form="♂ (male)"]
  R9 = Resistor [tolerance=±5% resistance=470 package=THT]
  J30 = male pin header, 3 pins [form="♂ (male)"]
  J31 = male pin header, 1 pin [form="♂ (male)"]
  R20 = Resistor [tolerance=±5% resistance=10k package=THT]  # not connected
  J38 = male pin header, 2 pins [form="♂ (male)"]
  R5 = Rotary Potentiometer (Small) [maximum_resistance=100kΩ package=THT]
  Arduino1 = Arduino Uno (Rev3)  # not connected
  J26 = male pin header, 3 pins [form="♂ (male)"]
  J25 = female pin header, 3 pins [form="♀ (female)"]
  J41 = female pin header, 2 pins [form="♀ (female)"]
  R6 = Rotary Potentiometer (Small) [maximum_resistance=100kΩ package=THT]
  LCD1 = LCD screen
  J46 = female pin header, 3 pins [form="♀ (female)"]
  J29 = female pin header, 3 pins [form="♀ (female)"]
  J39 = female pin header, 2 pins [form="♀ (female)"]
  J44 = female pin header, 3 pins [form="♀ (female)"]
  J51 = female pin header, 2 pins [form="♀ (female)"]

nets:
  N1: J1.pin1, LCD1.VDD
  N2: J1.pin2, LCD1.V0
  N3: J1.pin3, LCD1.RS
  N4: J1.pin4, LCD1.E
  N5: J1.pin5, LCD1.DB4
  N6: J1.pin6, LCD1.DB5
  N7: J1.pin7, LCD1.DB6
  N8: J1.pin8, LCD1.DB7
  N9: J1.pin9, LCD1.LED+
  N10: J1.pin10, LCD1.LED-
  N11: J2.pin1, M1.D
  N12: J2.pin2, M1.B
  N13: J2.pin3, M1.C
  N14: J2.pin4, M1.A
  N15: DRV2.EN, R2.leg2
  N16: DRV2.STEP, J10.pin1
  N17: DRV2.DIR, J10.pin2
  N18: DRV2.2B, J3.pin3
  N19: DRV2.2A, J3.pin4
  N20: DRV2.1A, J3.pin5
  N21: DRV2.1B, J3.pin6
  N22: C2.-, J3.pin1
  N23: J4.pin1, J5.pin1
  N24: J4.pin2, J5.pin2
  N25: J6.pin1, J7.pin2
  N26: J6.pin2, J7.pin1
  N27: J9.pin1, J8.pin1
  N28: J9.pin2, J8.pin2
  N29: J11.pin1, J14.pin7
  N30: J11.pin2, J14.pin6
  N31: J11.pin3, J14.pin5
  N32: J11.pin4, J14.pin4
  N33: J11.pin5, J14.pin3
  N34: J11.pin6, J14.pin2
  N35: J11.pin7, J14.pin1
  N36: J13.pin2, R3.Pin_0
  N37: J13.pin3, J12.pin2
  N38: J13.pin4, J12.pin3
  N39: J13.pin5, J12.pin4
  N40: J13.pin6, J12.pin5
  N41: J13.pin7, J12.pin6
  N42: J13.pin8, J12.pin7
  N43: J13.pin9, R2.wiper
  N44: R2.leg1, J18.pin1
  N45: J3.pin2, J30.pin3
  N46: J3.pin7, J17.pin3
  N47: J3.pin8, J18.pin3
  N48: J15.pin1, R5.leg1
  N49: J15.pin2, R5.wiper
  N50: J15.pin3, R5.leg2
  N51: J16.pin1, R6.leg1
  N52: J16.pin2, R6.wiper
  N53: J16.pin3, R6.leg2
  N54: J20.pin1, J21.pin2
  N55: J20.pin2, J21.pin1
  N56: J24.pin1, R9.Pin_0
  N57: J24.pin3, J22.pin1
  N58: J24.pin4, J22.pin2
  N59: J22.pin3, J45.pin3
  N60: J27.pin1, J47.pin1
  N61: J27.pin2, J47.pin2
  N62: J27.pin3, J47.pin3
  N63: J27.pin4, J47.pin4
  N64: J28.pin1, J32.pin1
  N65: T1.+Vs, J29.pin1
  N66: T1.Vout, J29.pin2
  N67: T1.GND, J29.pin3
  N68: S4.leg0, J41.pin1
  N69: S4.leg1, J41.pin2
  N70: R14.Pin_0, J37.pin2
  N71: R15.Pin_0, J36.pin2
  N72: R16.Pin_0, J35.pin2
  N73: R17.Pin_0, J34.pin2
  N74: R18.Pin_0, J38.pin2
  N75: R18.Pin_1, J33.pin2
  N76: R19.Pin_0, J38.pin1
  N77: R19.Pin_1, J33.pin1
  N78: LED1.cathode, J39.pin2
  N79: LED1.anode, J39.pin1
  N80: J48.pin2, J50.pin2
  N81: J49.pin2, J50.pin1
  N82: S5.leg0, J51.pin1
  N83: S5.leg1, J51.pin2
  N84: J52.pin1, J53.pin1
  N85: J52.pin2, J53.pin2
  N86: R22.Pin_1, J54.pin2
  N87: LED2.anode, J55.pin2
  N88: DRV3.EN, J58.pin1
  N89: DRV3.MS1, J58.pin2
  N90: DRV3.MS2, J58.pin3
  N91: DRV3.MS3, J58.pin4
  N92: DRV3.RST, J58.pin5
  N93: DRV3.SLP, J58.pin6
  N94: DRV3.STEP, J58.pin7, J59.pin1
  N95: DRV3.DIR, J58.pin8, J59.pin2
  N96: DRV3.VMOT, J57.pin1
  N97: DRV3.GNDMOT, J57.pin2
  N98: DRV3.2B, J56.pin3, J57.pin3
  N99: DRV3.2A, J56.pin4, J57.pin4
  N100: DRV3.1A, J56.pin5, J57.pin5
  N101: DRV3.1B, J56.pin6, J57.pin6
  N102: DRV3.VDD, J57.pin7
  N103: DRV3.GND, J57.pin8
  N104: J56.pin2, J71.pin3
  N105: J56.pin7, J61.pin3
  N106: J56.pin8, J62.pin3
  N107: J60.pin1, J62.pin2
  N108: J60.pin2, J61.pin2
  N109: R23.wiper, J63.pin9
  N110: J63.pin2, R26.Pin_0
  N111: J63.pin3, J64.pin2
  N112: J63.pin4, J64.pin3
  N113: J63.pin5, J64.pin4
  N114: J63.pin6, J64.pin5
  N115: J63.pin7, J64.pin6
  N116: J63.pin8, J64.pin7
  N117: J65.pin3, J68.pin3
  N118: J66.pin1, J73.pin1
  N119: J66.pin3, J68.pin1
  N120: J66.pin4, J68.pin2
  N121: J67.pin2, J70.pin2
  N122: J69.pin2, J70.pin1
  N123: J73.pin2, R25.Pin_1
  N124: J71.pin2, J72.pin1
  N125: J30.pin2, J31.pin1
  N126: J26.pin1, J25.pin3
  N127: J26.pin2, J25.pin2
  N128: J26.pin3, J25.pin1
  N129: LCD1.VSS, LCD1.R/W
  N130: J46.pin1, J44.pin2
  N131: J46.pin2, J44.pin3
  N132: J46.pin3, J44.pin1

notes:
  Nunchaku
  x2
  x4
  Negro 1, GRis 2
  Rojo 3

custom parts:
  A4983: Poloko A4983 Stepper Motor Control Breakout
